# Fritzing sketch Alphasense Arduino 16-Bit ADC (saved by Fritzing 0.7.11b)
breadboards: 1

parts:
  Arduino1 = Arduino
  Alphasense_ISB = male pin header, 6 pins [form="♂ (male)"]
  ADS1115 = male pin header, 10 pins [form="♂ (male)"]

nets:
  N1: Arduino1.GND, ADS1115.pin2
  N2: Arduino1.+5V, ADS1115.pin1
  N3: Arduino1.A4, ADS1115.pin4
  N4: Arduino1.A5, ADS1115.pin3
  6V: Alphasense_ISB.pin1
  GND: Alphasense_ISB.pin2, Alphasense_ISB.pin4, Alphasense_ISB.pin6
  N5: Alphasense_ISB.pin3, ADS1115.pin7
  N6: Alphasense_ISB.pin5, ADS1115.pin8
