# Fritzing sketch Alphasense Arduino (saved by Fritzing 0.7.11b)
breadboards: 1

parts:
  Arduino1 = Arduino
  Alphasense_ISB = male pin header, 6 pins [form="♂ (male)"]

nets:
  N1: Arduino1.A0, Alphasense_ISB.pin3
  N2: Arduino1.A1, Alphasense_ISB.pin5
  6V: Alphasense_ISB.pin1
  GND: Alphasense_ISB.pin2, Alphasense_ISB.pin4, Alphasense_ISB.pin6
